# Fritzing sketch Diagrama Protoboard (saved by Fritzing 1.0.4)
breadboards: 3

parts:
  Componente1 = InvenSense MPU6050
  LED1 = smd LED [color="Red (633nm)" package="0603 [SMD]"]
  J1 = RJ11 Jack [package=rj11-6]
  R1 = Resistor [tolerance=±5% resistance=220 package="0402 [SMD]"]
  Componente2 = InvenSense MPU6050
  LED2 = smd LED [color="Red (633nm)" package="0603 [SMD]"]
  J2 = RJ11 Jack [package=rj11-6]
  R2 = Resistor [tolerance=±5% resistance=220 package="0402 [SMD]"]
  J3 = RJ11 Jack [package=rj11-6]
  J4 = RJ11 Jack [package=rj11-6]
  LED3 = smd LED [color="Red (633nm)" package="0603 [SMD]"]
  R3 = Resistor [tolerance=±5% resistance=220 package="0402 [SMD]"]
  R4 = Resistor [tolerance=±5% resistance=220 package="0402 [SMD]"]
  LED4 = smd LED [color="Red (633nm)" package="0603 [SMD]"]
  U1 = SWITCH_SPDT [package=kps-1290]
  J5 = Basic Servo
  J6 = Basic Servo
  U2 = LIPO-1000mAh [package=lipo-1000]
  LED5 = smd LED [color="Red (633nm)" package="0603 [SMD]"]
  R5 = Resistor [tolerance=±5% resistance=220 package="0402 [SMD]"]
  Mod3 = Elecrow ESP32S WiFi/BLE Board V1.0 [part_number=ARS01119B]

nets:
  N1: Componente1.VCC, J1.1
  N2: Componente1.GND, J1.6
  N3: Componente1.SCL, J1.5
  N4: Componente1.SDA, J1.4
  N5: LED1.cathode, J1.2
  N6: LED1.anode, R1.Pin_1
  N7: J1.3, R1.Pin_0
  N8: Componente2.VCC, J2.1
  N9: Componente2.GND, J2.6
  N10: Componente2.SCL, J2.5
  N11: Componente2.SDA, J2.4
  N12: LED2.cathode, J2.2
  N13: LED2.anode, R2.Pin_1
  N14: J2.3, R2.Pin_0
  VCC: J3.1, J4.1, U1.P, J5.vcc, J6.vcc, R5.Pin_0, Mod3.pin38
  GND: J3.2, J3.6, J4.2, J4.6, LED3.cathode, LED4.cathode, U1.O, J5.gnd, J6.gnd, U2.-, LED5.cathode, Mod3.pin13, Mod3.pin19, Mod3.pin33, Mod3.pin37
  N15: J3.3, R4.Pin_0, Mod3.pin16
  N16: J3.4, J4.4, Mod3.pin14
  N17: J3.5, J4.5, Mod3.pin17
  N18: J4.3, R3.Pin_1, Mod3.pin15
  N19: LED3.anode, R3.Pin_0
  N20: R4.Pin_1, LED4.anode
  N21: U1.S, U2.+
  N22: J5.pulse, Mod3.pin27
  N23: J6.pulse, Mod3.pin26
  N24: LED5.anode, R5.Pin_1

custom parts:
  Elecrow ESP32S WiFi/BLE Board V1.0: The Elecrow ESP32S WiFi BLE Board V1.0 is one of the development boards created by Elecrow to evaluate the ESP-WROOM-32 module. It is based on the ESP32 microcontroller that boasts WiFi, Bluetooth, Ethernet and Low Power support all in a single chip. This board is 38 pins long (2x19) and 10 pins wide. Note in pcb view the mounting holes (2.8mm diameter) are only shown on silkscreen. If you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
